# Fritzing sketch biggreenbutton (saved by Fritzing 0.9.2b)
breadboards: 1

parts:
  Raspberry_Pi1 = Raspberry Pi B+
  Power_plug1 = Power plug
  LCD1 = LCD screen
  Part1 = Thermal Printer
  S1 = Round Pushbutton
  R1 = Resistor [tolerance=±5% resistance=10k package=THT]
  R2 = Rotary Potentiometer (Small) [maximum_resistance=100kΩ package=THT]
  GPS1 = Adafruit Ultimate GPS Breakout
  USBTTL1 = USB TTL Serial Cable
  LED1 = smd LED [color="Red (633nm)" package="0603 [SMD]"]

nets:
  N1: Raspberry_Pi1.GPIO17, LCD1.DB4
  N2: Raspberry_Pi1.GPIO22, LCD1.DB6
  GND: Raspberry_Pi1.GND, Power_plug1.GND, LCD1.VSS, LCD1.R/W, LCD1.LED-, Part1.GND#2, R2.leg1, LED1.cathode
  N3: Raspberry_Pi1.GPIO5, S1.leg1, R1.Pin_1
  N4: Raspberry_Pi1.GPIO21, LCD1.DB5
  N5: Raspberry_Pi1.GPIO25, LCD1.RS
  N6: Raspberry_Pi1.GPIO24, LCD1.E
  N7: Raspberry_Pi1.GPIO23, LCD1.DB3
  N8: Raspberry_Pi1.GPIO14, Part1.RXD
  N9: Raspberry_Pi1.5V, S1.leg0
  VCC: Power_plug1.VCC, LCD1.VDD, LCD1.LED+, Part1.VH, R1.Pin_0, R2.leg2
  N10: LCD1.V0, R2.wiper
  N11: GPS1.FIX, LED1.anode
  N12: GPS1.TX, USBTTL1.RX
  N13: GPS1.RX, USBTTL1.TX
  GND_2: GPS1.GND, USBTTL1.GND
  VIN: GPS1.VIN, USBTTL1.5V
